# Fritzing sketch Radon (saved by Fritzing 0.9.2b)
breadboards: 1

parts:
  Part1 = Arduino Uno (Rev3)
  J1 = Basic Servo
  J2 = Infrared Proximity Sensor

nets:
  N1: Part1.D9_PWM, J1.pulse
  N2: Part1.D5_PWM, J2.Vout
  VCC: Part1.5V, J1.vcc, J2.Vcc
  GND: Part1.GND, J1.gnd, J2.GND
